# Fritzing sketch connections (saved by Fritzing 0.9.4)
perfboards: 1

parts:
  MASTER = Arduino Pro Micro (Clone)
  MOLEX = COMPUTER-PERIPHERAL-POWER [package=computer-peripheral-power-ra]
  12_0v+ = Header 1 [package=smtso-256-et]
  3_3v+ = Header 1 [package=smtso-256-et]
  5_0v+ = Header 1 [package=smtso-256-et]
  GND- = Header 1 [package=smtso-256-et]
  J2 = COMPUTER-PERIPHERAL-POWER [package=computer-peripheral-power]
  R13 = Resistor [tolerance=±5% resistance=10k package=THT]
  R14 = Resistor [tolerance=±5% resistance=10k package=THT]
  R15 = Resistor [tolerance=±5% resistance=10k package=THT]
  R16 = Resistor [tolerance=±5% resistance=25k package=THT]
  R17 = Resistor [tolerance=±5% resistance=10k package=THT]
  R18 = Resistor [tolerance=±5% resistance=10k package=THT]
  Capacitor = Electrolytic Capacitor [capacitance=1µF package="100 mil [THT, electrolytic]"]
  SLAVE = Arduino Pro Micro (Clone)
  RTC_DS1307 = Tiny RTC
  JP1 = USB_MICROB_PLUG [package=micro-b-ra-th]
  Trimpot_10k = Breadboard Trimpot
  R7 = Resistor [tolerance=±5% resistance=10k package=THT]
  Thermistor_(temp°) = Temperature Sensor (Thermistor) [thermistor_type=PTC package=THT]
  LCD2 = 20x4 LCD display [part_number=2004A]
  <1_LCLK = female pin header, 1 pin [form="♀ (female)"]  # not connected
  SERIRQ_(v1_0)_16> = molex pin header, 1 pin [form=molex]  # not connected
  XBOX_LPC_DEBUG = molex pin header, 1 pin [form=molex]
  <13_SCL = molex pin header, 1 pin [form=molex]
  LAD1_10> = molex pin header, 1 pin [form=molex]  # not connected
  <3_LFRAME = molex pin header, 1 pin [form=molex]  # not connected
  LAD2_8> = molex pin header, 1 pin [form=molex]  # not connected
  PWR_(v1_6)_4> = molex pin header, 1 pin [form=molex]  # not connected
  5_0v_6> = molex pin header, 1 pin [form=molex]
  <15_3_3v = molex pin header, 1 pin [form=molex]  # not connected
  GND_2> = molex pin header, 1 pin [form=molex]
  GND_12> = molex pin header, 1 pin [form=molex]  # not connected
  <5_RST = molex pin header, 1 pin [form=molex]  # not connected
  <7_LAD3 = molex pin header, 1 pin [form=molex]  # not connected
  SDA_14> = molex pin header, 1 pin [form=molex]
  <11_LAD0 = molex pin header, 1 pin [form=molex]  # not connected
  <9_3_3v = molex pin header, 1 pin [form=molex]  # not connected

nets:
  N1: MASTER.TXO, SLAVE.RXI
  N2: MASTER.RXI, SLAVE.TXO
  GND: MASTER.GND, MOLEX.GND, Capacitor.-, SLAVE.GND, RTC_DS1307.GND, Trimpot_10k.PIN1, R7.Pin_0, LCD2.Vss, LCD2.R/W, LCD2.K_-
  N3: MASTER.D2, SDA_14>.pin1
  N4: MASTER.D3, <13_SCL.pin1
  N5: MASTER.D4, LCD2.Vo
  N6: MASTER.D5, LCD2.RS
  N7: MASTER.D6, LCD2.E
  N8: MASTER.D7, LCD2.DB4
  N9: MASTER.D9, R7.Pin_1, Thermistor_(temp°).pin_1
  N10: MASTER.D10, LCD2.A_+
  N11: MASTER.D16, LCD2.DB7
  N12: MASTER.D14, LCD2.DB5
  N13: MASTER.D15, LCD2.DB6
  N14: MASTER.A0, Trimpot_10k.PIN2
  N15: MASTER.A1, R13.Pin_0, R15.Pin_0
  N16: MASTER.A2, R14.Pin_0, R17.Pin_0
  N17: MASTER.A3, R16.Pin_0, R18.Pin_0
  VCC: MASTER.VCC, Trimpot_10k.PIN3, Thermistor_(temp°).pin_0, LCD2.Vdd
  N18: MOLEX.5V, R13.Pin_1, Capacitor.+, SLAVE.RAW
  N19: MOLEX.12V, R16.Pin_1
  N20: MOLEX.NC, R17.Pin_1
  N21: 12_0v+.1, J2.12V
  N22: 3_3v+.1, J2.NC
  N23: 5_0v+.1, J2.5V
  N24: GND-.1, J2.GND
  N25: R14.Pin_1, R18.Pin_1
  N26: SLAVE.D2, RTC_DS1307.SDA
  N27: SLAVE.D3, RTC_DS1307.SCL
  VCC_2: SLAVE.VCC, RTC_DS1307.VCC
  N28: JP1.VCC, 5_0v_6>.pin1
  N29: JP1.D+, XBOX_LPC_DEBUG.pin1, GND_2>.pin1

notes:
  XBOX PSU
  Required resistors
  for reading voltages
  3.3v -> 2x10kΩ
  5.0v -> 2x10kΩ
  12.0v -> 1x10kΩ -> (-)
  1x25kΩ -> (+)
  WARNING: Respect order for 12.0v see yellow wire with 25kΩ.
  Because your pro micro risk to die.

custom parts:
  Tiny RTC: Tiny RTC I2C module DS1370Z RTC and AT24C32 EEPROM
  20x4 LCD display: 20x4 character display. CHECK LED POLARITY BEFORE CONNECTING POWER Some versions of the dispaly have the polarity of the LED pins "A" and "K" reversed.
