# Fritzing sketch lpc_to_master (saved by Fritzing 0.9.3b)

parts:
  MASTER = Arduino Pro Micro (Clone)
  JP1 = USB_MICROB_PLUG [package=micro-b-ra-th]
  <1_LCLK = female pin header, 1 pin [form="♀ (female)"]  # not connected
  SERIRQ_(v1_0)_16> = molex pin header, 1 pin [form=molex]  # not connected
  XBOX_LPC_DEBUG = molex pin header, 1 pin [form=molex]
  <13_SCL = molex pin header, 1 pin [form=molex]
  LAD1_10> = molex pin header, 1 pin [form=molex]  # not connected
  <3_LFRAME = molex pin header, 1 pin [form=molex]  # not connected
  LAD2_8> = molex pin header, 1 pin [form=molex]  # not connected
  PWR_(v1_6)_4> = molex pin header, 1 pin [form=molex]  # not connected
  5_0v_6> = molex pin header, 1 pin [form=molex]
  <15_3_3v = molex pin header, 1 pin [form=molex]  # not connected
  GND_2> = molex pin header, 1 pin [form=molex]
  GND_12> = molex pin header, 1 pin [form=molex]  # not connected
  <5_RST = molex pin header, 1 pin [form=molex]  # not connected
  <7_LAD3 = molex pin header, 1 pin [form=molex]  # not connected
  SDA_14> = molex pin header, 1 pin [form=molex]
  <11_LAD0 = molex pin header, 1 pin [form=molex]  # not connected
  <9_3_3v = molex pin header, 1 pin [form=molex]  # not connected

nets:
  N1: MASTER.D2, SDA_14>.pin1
  N2: MASTER.D3, <13_SCL.pin1
  N3: JP1.VCC, 5_0v_6>.pin1
  N4: JP1.D+, XBOX_LPC_DEBUG.pin1, GND_2>.pin1

notes:
  LPC pin 14 to micro pin 2
  LPC pin 13 to micro pin 3
  USB Power 5v
  From LCP or other place.
  Ex: Controller Port, Molex...
