# Fritzing sketch master_lcd (saved by Fritzing 0.9.3b)

parts:
  MASTER = Arduino Pro Micro (Clone)
  Thermistor_(temp°) = Temperature Sensor (Thermistor) [thermistor_type=PTC package=THT]
  Resistor = Resistor [tolerance=±5% resistance=10k package=THT]
  POT_10k = Breadboard Trimpot
  LCD2 = 20x4 LCD display [part_number=2004A]

nets:
  GND: MASTER.GND, Resistor.Pin_0, POT_10k.PIN1, LCD2.Vss, LCD2.R/W, LCD2.K_-
  N1: MASTER.D4, LCD2.Vo
  N2: MASTER.D5, LCD2.RS
  N3: MASTER.D6, LCD2.E
  N4: MASTER.D7, LCD2.DB4
  N5: MASTER.D9, Thermistor_(temp°).pin_1, Resistor.Pin_1
  N6: MASTER.D10, LCD2.A_+
  N7: MASTER.D16, LCD2.DB7
  N8: MASTER.D14, LCD2.DB5
  N9: MASTER.D15, LCD2.DB6
  N10: MASTER.A0, POT_10k.PIN2
  VCC: MASTER.VCC, Thermistor_(temp°).pin_0, POT_10k.PIN3, LCD2.Vdd

notes:
  LCD to pin Micro
  VO to pin 4
  RS to pin 5
  EN to pin 6
  D4 to pin 7
  D5 to pin 14
  D6 to pin 15
  D7 to pin 16
  A+ to pin 10
  VSS to pin GND and POT pin 3
  VDD to pin VCC and POT pin 1
  POT pin 2 to pin A0
  Thermistor to pin 9
  Note
  Potentiometer (POT) control contrast and backlight in same time

custom parts:
  20x4 LCD display: 20x4 character display. CHECK LED POLARITY BEFORE CONNECTING POWER Some versions of the dispaly have the polarity of the LED pins "A" and "K" reversed.
