# Fritzing sketch molex (saved by Fritzing 0.9.3b)

parts:
  R19 = Resistor [tolerance=±5% resistance=10k package=THT]
  12_0v+ = Header 1 [package=smtso-256-et]
  MOLEX = COMPUTER-PERIPHERAL-POWER [package=computer-peripheral-power-ra]
  SLAVE = Arduino Pro Micro (Clone)
  MASTER = Arduino Pro Micro (Clone)
  R20 = Resistor [tolerance=±5% resistance=10k package=THT]
  R21 = Resistor [tolerance=±5% resistance=10k package=THT]
  5_0v+ = Header 1 [package=smtso-256-et]
  R22 = Resistor [tolerance=±5% resistance=25k package=THT]
  GND- = Header 1 [package=smtso-256-et]
  R23 = Resistor [tolerance=±5% resistance=10k package=THT]
  R24 = Resistor [tolerance=±5% resistance=10k package=THT]
  3_3v+ = Header 1 [package=smtso-256-et]
  Capacitor_minimum_220uf_6_3v = Electrolytic Capacitor [capacitance=1µF package="100 mil [THT, electrolytic]"]
  Femele_♀_|_Male_♂ = COMPUTER-PERIPHERAL-POWER [package=computer-peripheral-power]

nets:
  N1: R19.Pin_1, MOLEX.5V, SLAVE.RAW, Capacitor_minimum_220uf_6_3v.+
  N2: 12_0v+.1, Femele_♀_|_Male_♂.12V
  N3: MOLEX.12V, R22.Pin_1
  GND: MOLEX.GND, SLAVE.GND, MASTER.GND, R20.Pin_1, R21.Pin_1, R24.Pin_1, Capacitor_minimum_220uf_6_3v.-
  N4: MOLEX.NC, R23.Pin_1
  N5: MASTER.A1, R21.Pin_0
  N6: MASTER.A2, R23.Pin_0
  N7: MASTER.A3, R24.Pin_0
  N8: 5_0v+.1, Femele_♀_|_Male_♂.5V
  N9: GND-.1, Femele_♀_|_Male_♂.GND
  N10: 3_3v+.1, Femele_♀_|_Male_♂.NC

notes:
  XBOX PSU
  Required resistors
  for reading voltages
  3.3v -> 2x10kΩ
  5.0v -> 2x10kΩ
  12.0v -> 1x10kΩ -> (-)
  1x25kΩ -> (+)
  WARNING: Respect order for 12.0v see yellow wire with 25kΩ.
  Because your pro micro risk to die.
