# Fritzing sketch custom_pcb (saved by Fritzing 0.9.4)
perfboards: 1

parts:
  Composant1 = Arduino Pro Micro (Clone)
  Composant2 = Arduino Pro Micro (Clone)
  Composant3 = Adafruit DS1307 RTC Breakout [part_number="Adafruit #264"]
  U2 = Hirose DF13 Series Header [part_number=DF13#-4P-1.25V package=DF13C-4P-1.25V]
  R19 = Resistor [tolerance=±5% resistance=10k package=THT]
  R20 = Resistor [tolerance=±5% resistance=10k package=THT]
  R21 = Resistor [tolerance=±5% resistance=10k package=THT]
  R22 = Resistor [tolerance=±5% resistance=25k package=THT]
  R23 = Resistor [tolerance=±5% resistance=10k package=THT]
  R24 = Resistor [tolerance=±5% resistance=10k package=THT]
  J4 = double row male pin header, 2 pins [form="♂ (male)"]  # not connected
  C1 = Electrolytic Capacitor [capacitance=1µF package="100 mil [THT, electrolytic]"]
  Thermistor_(temp°)1 = Temperature Sensor (Thermistor) [thermistor_type=PTC package=THT]
  R25 = Resistor [tolerance=±5% resistance=10k package=THT]
  LCD2 = 20x4 LCD display [part_number=2004A]
  POT3 = Breadboard Trimpot
  J12 = female pin header, 16 pins [form="♀ (female)"]
  J11 = male pin header, 16 pins [form="♂ (male)"]  # not connected

nets:
  N1: Composant1.TXO, Composant2.RXI
  N2: Composant1.RXI, Composant2.TXO
  GND: Composant1.GND, Composant2.GND, Composant3.GND, U2.3, R20.Pin_1, R21.Pin_1, R23.Pin_1, C1.-, R25.Pin_1
  N3: Composant1.D9, Thermistor_(temp°)1.pin_1, R25.Pin_0
  N4: Composant1.A0, POT3.PIN2
  N5: Composant1.A1, R19.Pin_0, R21.Pin_0
  N6: Composant1.A2, R20.Pin_0, R24.Pin_0
  N7: Composant1.A3, R22.Pin_0, R23.Pin_0
  N8: Composant1.VCC, Thermistor_(temp°)1.pin_0
  N9: Composant2.D2, Composant3.SDA
  N10: Composant2.D3, Composant3.SCL
  VCC: Composant2.VCC, Composant3.VCC
  N11: Composant2.RAW, U2.4, R19.Pin_1, C1.+
  N12: U2.1, R22.Pin_1
  N13: U2.2, R24.Pin_1
  N14: LCD2.Vss, LCD2.R/W, LCD2.K_-, POT3.PIN1, J12.pin1, J12.pin5, J12.pin16
  N15: LCD2.Vdd, POT3.PIN3, J12.pin2
  N16: LCD2.Vo, J12.pin3
  N17: LCD2.RS, J12.pin4
  N18: LCD2.E, J12.pin6
  N19: LCD2.DB3, LCD2.DB4, J12.pin11
  N20: LCD2.DB5, J12.pin12
  N21: LCD2.DB6, J12.pin13
  N22: LCD2.DB7, J12.pin14
  N23: LCD2.A_+, J12.pin15

notes:
  LCD to pin Micro
  VO pin 4
  RS pin 5
  EN pin 6
  D4 pin 7
  D5 pin 14
  D6 pin 15
  D7 pin 16
  A+ pin 10
  VSS pin GND
  VDD pin VCC
  POT pin A0

custom parts:
  Adafruit DS1307 RTC Breakout: This is a great battery-backed real time clock (RTC) that allows your microcontroller project to keep track of time even if it is reprogrammed, or if the power is lost. Perfect for datalogging, clock-building, time stamping, timers and alarms, etc. The DS1307 is the most popular RTC - but it requires 5V power to work (although we've used it with 5V power and 3.3V logic successfully) PCB &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
  20x4 LCD display: 20x4 character display. CHECK LED POLARITY BEFORE CONNECTING POWER Some versions of the dispaly have the polarity of the LED pins "A" and "K" reversed.
