# Fritzing sketch lcd_to_header (saved by Fritzing 0.9.3b)

parts:
  DB5 = Header 1 [package=smtso-256-et]
  EN = Header 1 [package=smtso-256-et]
  VO-VE = Header 1 [package=smtso-256-et]
  VSS = Header 1 [package=smtso-256-et]
  RS = Header 1 [package=smtso-256-et]
  DB4 = Header 1 [package=smtso-256-et]
  DB7 = Header 1 [package=smtso-256-et]
  DB6 = Header 1 [package=smtso-256-et]
  POT = Header 1 [package=smtso-256-et]
  A+ = Header 1 [package=smtso-256-et]
  LCD1 = 20x4 LCD display [part_number=2004A]
  VDD = Header 1 [package=smtso-256-et]
  1> = Header 1 [package=smtso-256-et]
  POT1 = Breadboard Trimpot
  Male_♂ = molex pin header, 5 pins [form=molex]  # not connected
  Femele_♀ = molex pin header, 5 pins [form=molex]  # not connected
  J7 = molex pin header, 1 pin [form=molex]  # not connected

nets:
  N1: DB5.1, LCD1.DB5
  N2: EN.1, LCD1.E
  N3: VO-VE.1, LCD1.Vo
  N4: VSS.1, LCD1.Vss, LCD1.R/W, LCD1.K_-, POT1.PIN1
  N5: RS.1, LCD1.RS
  N6: DB4.1, LCD1.DB4
  N7: DB7.1, LCD1.DB7
  N8: DB6.1, LCD1.DB6
  N9: POT.1, POT1.PIN2
  N10: A+.1, LCD1.A_+
  N11: LCD1.Vdd, VDD.1, 1>.1, POT1.PIN3

notes:
  LCD to pin Micro
  VO pin 4
  RS pin 5
  EN pin 6
  D4 pin 7
  D5 pin 14
  D6 pin 15
  D7 pin 16
  A+ pin 10
  VSS pin GND
  VDD pin VCC
  POT pin A0

custom parts:
  20x4 LCD display: 20x4 character display. CHECK LED POLARITY BEFORE CONNECTING POWER Some versions of the dispaly have the polarity of the LED pins "A" and "K" reversed.
