# Fritzing sketch not_great_work (saved by Fritzing 0.9.3b)
perfboards: 1

parts:
  12v|3v|GND|5v = COMPUTER-PERIPHERAL-POWER [package=computer-peripheral-power-ra]
  Composant1 = Arduino Pro Micro (Clone)
  R1 = Resistor [tolerance=±5% resistance=10k package=THT]
  R2 = Resistor [tolerance=±5% resistance=10k package=THT]
  R5 = Resistor [tolerance=±5% resistance=10k package=THT]
  R6 = Resistor [tolerance=±5% resistance=10k package=THT]
  Thermistor_(temp°) = Temperature Sensor (Thermistor) [thermistor_type=NTC package=THT]
  R9 = Resistor [tolerance=±5% resistance=10k package=THT]
  Reset = Pushbutton [package="[THT]"]
  R10 = Resistor [tolerance=±5% resistance=25k package=THT]
  R11 = Resistor [tolerance=±5% resistance=10k package=THT]
  RTC_DS1307 = Tiny RTC
  TO_LCD = molex pin header, 7 pins [form=molex]  # not connected
  J5 = molex pin header, 7 pins [form=molex]
  SDA_|_SCL = molex pin header, 2 pins [form=molex]  # not connected
  Jumper_PWR = molex pin header, 2 pins [form=molex]  # not connected
  C1 = Electrolytic Capacitor [capacitance=100μF package="0807 [SMD, electrolytic]"]
  <15_3_3v = molex pin header, 1 pin [form=molex]  # not connected
  <13_SCL = molex pin header, 1 pin [form=molex]
  <11_LAD3 = molex pin header, 1 pin [form=molex]  # not connected
  <9_3_3v = molex pin header, 1 pin [form=molex]  # not connected
  <3_LFRAME = molex pin header, 1 pin [form=molex]  # not connected
  <5_RST = molex pin header, 1 pin [form=molex]  # not connected
  <7_LAD4 = molex pin header, 1 pin [form=molex]  # not connected
  LAD1_10> = molex pin header, 1 pin [form=molex]  # not connected
  GND_12> = molex pin header, 1 pin [form=molex]  # not connected
  SDA_14> = molex pin header, 1 pin [form=molex]
  SERIRQ_(v1_0)_16> = molex pin header, 1 pin [form=molex]  # not connected
  GND_2> = molex pin header, 1 pin [form=molex]  # not connected
  5_0v_6> = molex pin header, 1 pin [form=molex]  # not connected
  LAD2_8> = molex pin header, 1 pin [form=molex]  # not connected
  <1_LCLK = female pin header, 1 pin [form="♀ (female)"]  # not connected
  XBOX_LPC_DEBUG = molex pin header, 1 pin [form=molex]  # not connected
  PWR_(v1_6)_4> = molex pin header, 1 pin [form=molex]  # not connected
  R15 = Resistor [tolerance=±5% resistance=220 package=THT]
  R14 = Resistor [tolerance=±5% resistance=220 package=THT]

nets:
  N1: 12v|3v|GND|5v.5V, R1.Pin_1, C1.+
  N2: 12v|3v|GND|5v.12V, R10.Pin_1
  GND: 12v|3v|GND|5v.GND, Composant1.GND, R2.Pin_1, R6.Pin_1, R9.Pin_0, Reset.Pin_3, Reset.Pin_4, R11.Pin_1, RTC_DS1307.GND, C1.-
  N3: 12v|3v|GND|5v.NC, R5.Pin_1
  N4: Composant1.D2, RTC_DS1307.SDA#8
  N5: Composant1.D3, RTC_DS1307.SCL#7
  N6: Composant1.D8, R15.Pin_1, R14.Pin_1
  N7: Composant1.D9, R9.Pin_1
  N8: Composant1.A1, R1.Pin_0, R2.Pin_0
  N9: Composant1.A2, R5.Pin_0, R6.Pin_0
  N10: Composant1.A3, R10.Pin_0, R11.Pin_0
  VCC: Composant1.VCC, Thermistor_(temp°).pin_0, RTC_DS1307.VCC, J5.pin7
  N11: Composant1.RST, Reset.Pin_1, Reset.Pin_2
  N12: RTC_DS1307.SCL#1, <13_SCL.pin1
  N13: RTC_DS1307.SDA#2, SDA_14>.pin1

custom parts:
  Tiny RTC: Tiny RTC I2C module DS1370Z RTC and AT24C32 EEPROM
