# Fritzing sketch serial1 (saved by Fritzing 0.9.3b)

parts:
  SLAVE = Arduino Pro Micro (Clone)
  MASTER = Arduino Pro Micro (Clone)

nets:
  N1: SLAVE.TXO, MASTER.RXI
  N2: SLAVE.RXI, MASTER.TXO
  GND: SLAVE.GND, MASTER.GND

notes:
  Master TX pin to Slave RX pin
  Master RX pin to Slave TX pin
  GND to GND
