# Fritzing sketch slave_rtc (saved by Fritzing 0.9.3b)

parts:
  SLAVE = Arduino Pro Micro (Clone)
  RTC_DS1307 = Tiny RTC

nets:
  GND: SLAVE.GND, RTC_DS1307.GND
  N1: SLAVE.D2, RTC_DS1307.SDA
  N2: SLAVE.D3, RTC_DS1307.SCL
  VCC: SLAVE.VCC, RTC_DS1307.VCC

notes:
  RTC to pin Micro
  GND to GND
  VCC to VCC
  SDA to pin 2
  SCL to pin 3

custom parts:
  Tiny RTC: Tiny RTC I2C module DS1370Z RTC and AT24C32 EEPROM
